// Logisim project 2bitMultiplier.circ as structural Verilog: 2 circuits, main circuit main
module main (
  input  a1,
  input  a0,
  input  b1,
  input  b0,
  output out_5,
  output out_6,
  output out_7,
  output out_8
);

  wire and_2_out, and_3_out, and_4_out, ha_1_carry;

  Hex_Digit_Display hex_digit_display_1 (.value({2'b00, a1, a0}));  // open: dp
  Hex_Digit_Display hex_digit_display_2 (.value({2'b00, b1, b0}));  // open: dp
  and and_1 (out_8, a0, b0);
  and and_2 (and_2_out, a1, b0);
  and and_3 (and_3_out, a0, b1);
  and and_4 (and_4_out, b1, a1);
  Hex_Digit_Display hex_digit_display_3 (.value({out_5, out_6, out_7, out_8}));  // open: dp
  HA ha_1 (.B(and_2_out), .A(and_3_out), .SUM(out_7), .CARRY(ha_1_carry));
  HA ha_2 (.B(ha_1_carry), .A(and_4_out), .SUM(out_6), .CARRY(out_5));
endmodule

module HA (
  input  A,
  input  B,
  output SUM,
  output CARRY
);

  xor xor_1 (SUM, A, B);
  and and_1 (CARRY, A, B);
endmodule
