// Logisim project function_ledC.circ as structural Verilog: 2 circuits, main circuit functionC_raw
module functionC_raw (
  input  P,
  input  Q,
  input  R,
  input  S,
  output c
);

  wire and_1_out, and_2_out, and_3_out, and_4_out, and_5_out, not_1_out, not_2_out, not_3_out;

  not not_1 (not_1_out, P);
  not not_2 (not_2_out, Q);
  not not_3 (not_3_out, R);
  and and_1 (and_1_out, not_1_out, Q);
  and and_2 (and_2_out, P, not_2_out);
  and and_3 (and_3_out, not_3_out, S);
  and and_4 (and_4_out, not_1_out, not_3_out);
  and and_5 (and_5_out, not_1_out, S);
  or or_1 (c, and_1_out, and_2_out, and_3_out, and_4_out, and_5_out);
endmodule

module functionC_optimized (
  input  in3,
  input  in2,
  input  in1,
  input  in0,
  output c
);

  wire and_1_out, nand_1_out, nor_1_out, xor_1_out;

  nand nand_1 (nand_1_out, in3, in1);
  xor xor_1 (xor_1_out, in3, in2);
  nor nor_1 (nor_1_out, in3, in1);
  and and_1 (and_1_out, nand_1_out, in0);
  or or_1 (c, xor_1_out, and_1_out, nor_1_out);
endmodule
