// Logisim project AND_Gated_D_Latch.circ as structural Verilog: 1 circuit, main circuit main
module main (
  input  D,
  input  E,
  output NQ,
  output Q
);

  wire and_1_out, and_2_out, not_1_out;

  not not_1 (not_1_out, D);
  and and_1 (and_1_out, D, E);
  and and_2 (and_2_out, E, not_1_out);
  nor nor_1 (NQ, and_1_out, Q);
  nor nor_2 (Q, NQ, and_2_out);
endmodule
