// Logisim project dFlipFlop.circ as structural Verilog: 1 circuit, main circuit main
module main (
  input  D,
  output Q
);

  wire not_1_out;

  not not_1 (not_1_out, D);
  D_Flip_Flop d_ff_1 (.clk(D), .D(not_1_out), .Q(Q));  // open: Qn, preset, reset
endmodule
