// Logisim project NAND_GatedSR_Latch.circ as structural Verilog: 1 circuit, main circuit main
module main (
  input  R,
  input  Enable,
  input  S,
  output Q,
  output NQ
);

  wire and_1_out, and_2_out;

  and and_1 (and_1_out, R, Enable);
  and and_2 (and_2_out, Enable, S);
  nor nor_1 (Q, and_1_out, NQ);
  nor nor_2 (NQ, Q, and_2_out);
endmodule
