// Logisim project SR_AND_OR_Latch.circ as structural Verilog: 1 circuit, main circuit main
module main (
  input  S,
  input  R,
  output Q
);

  wire not_1_out, or_1_out;

  or or_1 (or_1_out, Q, S);
  not not_1 (not_1_out, R);
  and and_1 (Q, or_1_out, not_1_out);
endmodule
