// Logisim project SchemFA.circ as structural Verilog: 1 circuit, main circuit FA_by_HA_blocks
module FA_by_HA_blocks (
  input  A,
  input  B,
  input  in_3,
  output sum,
  output Cout
);

  wire halfadder_1_p3, halfadder_1_p4, halfadder_2_p4;

  // HalfAdder halfadder_1: pin names not known; wires that end beside it: A, B, halfadder_1_p3, halfadder_1_p4
  // HalfAdder halfadder_2: pin names not known; wires that end beside it: halfadder_1_p3, in_3, sum, halfadder_2_p4
  or or_1 (Cout, halfadder_2_p4, halfadder_1_p4);
endmodule
