// Logisim project SchemHalfAdder.circ as structural Verilog: 1 circuit, main circuit HalfAdder
module HalfAdder (
  input  A,
  input  B,
  output SUM,
  output CARRY
);

  xor xor_1 (SUM, A, B);
  and and_1 (CARRY, A, B);
endmodule
