// Logisim project FullSubtractor.circ as structural Verilog: 1 circuit, main circuit main
module main (
  input  A,
  input  B,
  input  Bin,
  output DIFFERENCE,
  output BORROW
);

  wire and_1_out, and_2_out, not_1_out, xor_1_out, xor_2_out;

  not not_1 (not_1_out, A);
  xor xor_1 (xor_1_out, B, Bin);
  and and_1 (and_1_out, B, Bin);
  xor xor_2 (xor_2_out, A, B);
  and and_2 (and_2_out, not_1_out, xor_1_out);
  xor xor_3 (DIFFERENCE, xor_2_out, Bin);
  or or_1 (BORROW, and_2_out, and_1_out);
endmodule
