// Logisim project Three_way_light_control.circ as structural Verilog: 3 circuits, main circuit SOP
module SOP (
  input  x1,
  input  x2,
  input  x3,
  output f
);

  wire and_1_out, and_2_out, and_3_out, and_4_out, not_1_out, not_2_out, not_3_out;

  not not_1 (not_1_out, x1);
  not not_2 (not_2_out, x2);
  not not_3 (not_3_out, x3);
  and and_1 (and_1_out, not_1_out, not_2_out, x3);
  and and_2 (and_2_out, not_1_out, x2, not_3_out);
  and and_3 (and_3_out, x1, not_2_out, not_3_out);
  and and_4 (and_4_out, x1, x2, x3);
  or or_1 (f, and_1_out, and_2_out, and_3_out, and_4_out);
endmodule

module optimized (
  input  x1,
  input  x2,
  input  x3,
  output f
);

  wire xor_1_out;

  xor xor_1 (xor_1_out, x2, x3);
  xor xor_2 (f, x1, xor_1_out);
endmodule

module POS (
  input  x1,
  input  x2,
  input  x3,
  output f
);

  wire not_1_out, not_2_out, not_3_out, or_1_out, or_2_out, or_3_out, or_4_out;

  not not_1 (not_1_out, x1);
  not not_2 (not_2_out, x2);
  not not_3 (not_3_out, x3);
  or or_1 (or_1_out, x1, x2, x3);
  or or_2 (or_2_out, x1, not_2_out, not_3_out);
  or or_3 (or_3_out, not_1_out, x2, not_3_out);
  or or_4 (or_4_out, not_1_out, not_2_out, x3);
  and and_1 (f, or_1_out, or_2_out, or_3_out, or_4_out);
endmodule
